// Logisim project ps2_interface_placuta13.circ as structural Verilog
module main (
  input  sys_clk,
  input  Reset,
  input  ps2_clk,
  input  ps2_ser,
  output [7:0] cathodes,
  output annode_0,
  output annode_1,
  output annode_2,
  output annode_3,
  output annode_4,
  output annode_5,
  output annode_6,
  output annode_7
);

  wire counter16bit_1_tcount, cu_outputs_1_clear, cu_outputs_1_en_shift, eo_verif_unit_1_valid, not_1_out,
       validation_unit_1_valid;
  wire [2:0] counter3bit_1_value, cu_rom_1_content;
  wire [3:0] mux8to1whichis1bit_1_output;
  wire [5:0] clk_sync_1_synced;
  wire [7:0] decoder7sd_1_content, display_buffer_1_data_out0, display_buffer_1_data_out1,
       display_buffer_1_data_out2, display_buffer_1_data_out3, display_buffer_1_data_out4,
       display_buffer_1_data_out5, display_buffer_1_data_out6, display_buffer_1_data_out7,
       shift_register_11bit_1_q8;
  wire [10:0] shift_register_11bit_1_q;

  clk_sync clk_sync_1 (.sys_clk(sys_clk), .ps2_clk(ps2_clk), .synced(clk_sync_1_synced[0]));
  CU_ROM cu_rom_1 (.address(mux8to1whichis1bit_1_output), .content(cu_rom_1_content));
  d_flip_flop d_flip_flop_1 (.clock(sys_clk), .d(cu_rom_1_content[0]), .q(mux8to1whichis1bit_1_output[0]));
  d_flip_flop d_flip_flop_2 (.clock(sys_clk), .d(cu_rom_1_content[1]), .q(mux8to1whichis1bit_1_output[1]));
  d_flip_flop d_flip_flop_3 (.clock(sys_clk), .d(cu_rom_1_content[2]), .q(mux8to1whichis1bit_1_output[2]));
  modulo11_counter modulo11_counter_1 (.clk(clk_sync_1_synced[0]), .reset(Reset), .tc(clk_sync_1_synced[4]));
  MUX8TO1WHICHIS1BIT mux8to1whichis1bit_1 (
    .val({2'b00, clk_sync_1_synced[5:2], clk_sync_1_synced[4], clk_sync_1_synced[0]}),
    .sel(mux8to1whichis1bit_1_output[2:0]), .\output (mux8to1whichis1bit_1_output[3]));
  shift_register_11bit shift_register_11bit_1 (
    .clk(clk_sync_1_synced[0]), .sin(ps2_ser), .reset(Reset), .q(shift_register_11bit_1_q),
    .q8(shift_register_11bit_1_q8));
  CU_Outputs cu_outputs_1 (
    .state(mux8to1whichis1bit_1_output[2:0]), .en_shift(cu_outputs_1_en_shift), .clear(cu_outputs_1_clear));
  decoder7sd decoder7sd_1 (.address(shift_register_11bit_1_q8), .content(decoder7sd_1_content));
  and and_1 (clk_sync_1_synced[2], validation_unit_1_valid, not_1_out);
  validation_unit validation_unit_1 (.c(shift_register_11bit_1_q), .valid(validation_unit_1_valid));
  not not_1 (not_1_out, eo_verif_unit_1_valid);
  eo_verif_unit eo_verif_unit_1 (.c(shift_register_11bit_1_q), .valid(eo_verif_unit_1_valid));
  fo_verif_unit fo_verif_unit_1 (.c(shift_register_11bit_1_q), .valid(clk_sync_1_synced[3]));
  enter_verif_unit enter_verif_unit_1 (.c(shift_register_11bit_1_q), .valid(clk_sync_1_synced[5]));
  display_buffer display_buffer_1 (
    .data_in(decoder7sd_1_content), .enable(cu_outputs_1_en_shift), .clk(sys_clk),
    .reset(cu_outputs_1_clear), .data_out0(display_buffer_1_data_out0),
    .data_out1(display_buffer_1_data_out1), .data_out2(display_buffer_1_data_out2),
    .data_out3(display_buffer_1_data_out3), .data_out4(display_buffer_1_data_out4),
    .data_out5(display_buffer_1_data_out5), .data_out6(display_buffer_1_data_out6),
    .data_out7(display_buffer_1_data_out7));
  counter16bit counter16bit_1 (.clock(sys_clk), .tCount(counter16bit_1_tcount));  // open: value
  counter3bit counter3bit_1 (.clock(sys_clk), .enable(counter16bit_1_tcount), .value(counter3bit_1_value));
  mux8to1_8bit mux8to1_8bit_1 (
    .in0(display_buffer_1_data_out0), .in1(display_buffer_1_data_out1), .in2(display_buffer_1_data_out2),
    .in3(display_buffer_1_data_out3), .in4(display_buffer_1_data_out4), .in5(display_buffer_1_data_out5),
    .in6(display_buffer_1_data_out6), .in7(display_buffer_1_data_out7), .sel(counter3bit_1_value),
    .y(cathodes));
  dmux8to1 dmux8to1_1 (
    .val(1'b0), .sel(counter3bit_1_value), .y0(annode_0), .y1(annode_1), .y2(annode_2), .y3(annode_3),
    .y4(annode_4), .y5(annode_5), .y6(annode_6), .y7(annode_7));

  // Notes on the sheet:
  //   clk
  //   reset
  //   ps2 clk
  //   ps2 ser
  //   to implement in the real circuit:
  //   add decoder 7sd, eliminate the d flip-flop
endmodule

// VHDL entity CU_ROM, as the project stores it:
LIBRARY ieee;
USE ieee.std_logic_1164.all;

ENTITY CU_ROM IS
  PORT (
  ------------------------------------------------------------------------------
  --Insert input ports below
    address        : IN  std_logic_vector(3 DOWNTO 0); -- input vector example
  ------------------------------------------------------------------------------
  --Insert output ports below
    content        : OUT std_logic_vector(2 DOWNTO 0)  -- output vector example
    );
END CU_ROM;

--------------------------------------------------------------------------------
--Complete your VHDL description below
--------------------------------------------------------------------------------

ARCHITECTURE TypeArchitecture OF CU_ROM IS

BEGIN

	process (address)
		begin
		case address is
		when "0000" => content <= "001";
		when "1000" => content <= "000";
		when "0001" => content <= "001";
		when "1001" => content <= "011";
		when "0010" => content <= "000";
		when "1010" => content <= "011";
		when "0011" => content <= "101";
		when "1011" => content <= "100";
		when "0101" => content <= "110";
		when "1101" => content <= "111";
		when "0100" => content <= "100";
		when "1100" => content <= "000";
		when "0110" => content <= "000";
		when "1110" => content <= "000";
		when "0111" => content <= "000";
		when "1111" => content <= "000";
		when others => content <= "000";

		end case;
	end process;
END TypeArchitecture;

// VHDL entity CU_Outputs, as the project stores it:
LIBRARY ieee;
USE ieee.std_logic_1164.all;

ENTITY CU_Outputs IS
  PORT (
	state 	: IN std_logic_vector(2 downto 0);
	en_shift 	: OUT std_logic;
	clear	: OUT std_logic
  );
END CU_Outputs;

ARCHITECTURE TypeArchitecture OF CU_Outputs IS

BEGIN

process(state) is
begin
	if state = "110" then 
		en_shift <= '1';
	else 
		en_shift <= '0';
	end if;
	if state = "111" then
		clear <= '1';
	else 
		clear <= '0';
	end if;
end process;
END TypeArchitecture;

// VHDL entity d_flip_flop, as the project stores it:
LIBRARY ieee;
USE ieee.std_logic_1164.all;

ENTITY d_flip_flop IS
  PORT (
  ------------------------------------------------------------------------------
  --Insert input ports below
    clock      : IN  std_logic;                    -- input bit example
    d        	: IN  std_logic; -- input vector example
  ------------------------------------------------------------------------------
  --Insert output ports below
    q        : OUT std_logic
    );
END d_flip_flop;

--------------------------------------------------------------------------------
--Complete your VHDL description below
--------------------------------------------------------------------------------

ARCHITECTURE TypeArchitecture OF d_flip_flop IS

BEGIN

	process(clock) is
	variable internal_state : std_logic := '0';
	begin
		if(rising_edge(clock)) then
			internal_state := d;
		end if;
		q <= internal_state;
	end process;
END TypeArchitecture;

// VHDL entity MUX8TO1WHICHIS1BIT, as the project stores it:
LIBRARY ieee;
USE ieee.std_logic_1164.all;

ENTITY MUX8TO1WHICHIS1BIT IS
  PORT (
  ------------------------------------------------------------------------------
  --Insert input ports below
    val        : IN  std_logic_vector(7 DOWNTO 0); -- input vector example
    sel 		: IN  std_logic_vector(2 downto 0); -- selection bit
  ------------------------------------------------------------------------------
  --Insert output ports below
    output        : OUT std_logic                -- output bit example
    );
END MUX8TO1WHICHIS1BIT;

--------------------------------------------------------------------------------
--Complete your VHDL description below
--------------------------------------------------------------------------------

ARCHITECTURE TypeArchitecture OF MUX8TO1WHICHIS1BIT IS

BEGIN

	process(val, sel)
		begin
			case sel is
			when "000" => output <= val(0);
			when "001" => output <= val(1);
			when "010" => output <= val(2);
			when "011" => output <= val(3);
			when "100" => output <= val(4);
			when "101" => output <= val(5);
			when "110" => output <= val(6);
			when "111" => output <= val(7);
			when others => output <= '0';
	end case;

	end process;
END TypeArchitecture;

// VHDL entity decoder7sd, as the project stores it:
-- Project :
-- File    :
-- Autor   :
-- Date    :
--
--------------------------------------------------------------------------------
-- Description :
--
--------------------------------------------------------------------------------

LIBRARY ieee;
USE ieee.std_logic_1164.all;

ENTITY decoder7sd IS
  PORT (
  ------------------------------------------------------------------------------
  --Insert input ports below
    address      : IN  std_logic_vector (7 downto 0);                    -- input bit example
  ------------------------------------------------------------------------------
  --Insert output ports below
    content        : OUT std_logic_vector (7 DOWNTO 0)  -- output vector example
    );
END decoder7sd;

--------------------------------------------------------------------------------
--Complete your VHDL description below
--------------------------------------------------------------------------------

ARCHITECTURE TypeArchitecture OF decoder7sd IS
BEGIN

	process(address)
		begin
			case address is 
				when x"16" => content <= b"01100000"; --1
				when x"1E" => content <= b"11011010"; --2
				when x"26" => content <= b"11110010"; --3
				when x"25" => content <= b"01100110"; --4
				when x"2E" => content <= b"10110110"; --5
				when x"36" => content <= b"10111110"; --6
				when x"3D" => content <= b"11100000"; --7
				when x"3E" => content <= b"11111110"; --8
				when x"46" => content <= b"11110110"; --9
				when x"45" => content <= b"11111100"; --0
				when x"15" => content <= b"11111101"; --q
				when x"44" => content <= b"11111100"; --o
				when x"1D" => content <= b"01111110"; --w
				when x"24" => content <= b"10011110"; --e
				when x"2D" => content <= b"00001010"; --small r
				when x"2C" => content <= b"00011110"; --small t
				when x"35" => content <= b"01110110"; --small y
				when x"3C" => content <= b"01111100"; --U
				when x"43" => content <= b"00001100"; --I
				when x"4D" => content <= b"11001110"; --P
				when x"1C" => content <= b"11101110"; --A
				when x"1B" => content <= b"10110110"; --S
				when x"23" => content <= b"11111100"; --D
				when x"2B" => content <= b"10001110"; --F
				when x"34" => content <= b"10111100"; --G
				when x"33" => content <= b"01101110"; --H
				when x"3B" => content <= b"01111000"; --J
				when x"42" => content <= b"10101110"; --K 
				when x"4B" => content <= b"00011100"; --L
				when x"1A" => content <= b"00001100"; --Z
				when x"22" => content <= b"10010010"; --x
				when x"21" => content <= b"10011100"; --C
				when x"2A" => content <= b"01010100"; --V
				when x"32" => content <= b"11111110"; --B
				when x"31" => content <= b"00101010"; --small N
				when x"3A" => content <= b"11010100"; --M
				when x"41" => content <= b"00000001"; --,
				when x"49" => content <= b"00000001"; --.

				when others =>content<=  b"00000000"; 
		end case;
	end process;
END TypeArchitecture;

// VHDL entity display_buffer, as the project stores it:
LIBRARY ieee;
USE ieee.std_logic_1164.all;

ENTITY display_buffer IS
  PORT (
    data_in	: IN std_logic_vector(7 downto 0);
    enable	: IN std_logic;
    clk		: IN std_logic;
    reset		: IN std_logic;

    data_out0	: OUT std_logic_vector(7 downto 0);
    data_out1	: OUT std_logic_vector(7 downto 0);
    data_out2	: OUT std_logic_vector(7 downto 0);
    data_out3	: OUT std_logic_vector(7 downto 0);
    data_out4	: OUT std_logic_vector(7 downto 0);
    data_out5	: OUT std_logic_vector(7 downto 0);
    data_out6	: OUT std_logic_vector(7 downto 0);
    data_out7	: OUT std_logic_vector(7 downto 0)
    );
END display_buffer;


ARCHITECTURE TypeArchitecture OF display_buffer IS

type t_Memory is array (7 downto 0) of std_logic_vector(7 downto 0);--type of data to store the contents of the shift register

BEGIN


process(clk) is
variable reg : t_Memory := (others => "00000000");
begin
	if(clk'event AND clk='0') then
		if(reset = '1') then
			reg := (others => "00000000");
		elsif(enable = '1') then
			reg := data_in & reg(7 downto 1);
		end if;
		data_out0 <= reg(0);
		data_out1 <= reg(1);
		data_out2 <= reg(2);
		data_out3 <= reg(3);
		data_out4 <= reg(4);
		data_out5 <= reg(5);
		data_out6 <= reg(6);
		data_out7 <= reg(7);
		 
	end if;
end process;

END TypeArchitecture;

// VHDL entity counter16bit, as the project stores it:
LIBRARY ieee;
USE ieee.std_logic_1164.all;

USE IEEE.NUMERIC_STD.ALL;

ENTITY counter16bit IS
  PORT (
  ------------------------------------------------------------------------------
  --Insert input ports below
    clock      : IN  std_logic;                    -- input bit example
  ------------------------------------------------------------------------------
  --Insert output ports below
  	value	   : OUT std_logic_vector (15 downto 0);
    tCount        : OUT std_logic                    -- output bit example
    );
END counter16bit;

--------------------------------------------------------------------------------
--Complete your VHDL description below
--------------------------------------------------------------------------------

ARCHITECTURE TypeArchitecture OF counter16bit IS

BEGIN


process(clock)
	variable internal_state : natural range 0 to 2**16-1 := 0;
	begin
	tCount <= '0';
	if(clock'event AND clock='1') then
		if(internal_state = 65535) then
			tCount <= '1';
			internal_state := 0;
		else
			tCount <= '0';
			internal_state := internal_state + 1;
		end if;
	end if;
	value <= std_logic_vector(to_unsigned(internal_state,16));
end process;

END TypeArchitecture;

// VHDL entity counter3bit, as the project stores it:
LIBRARY ieee;
USE ieee.std_logic_1164.all;

USE IEEE.NUMERIC_STD.ALL;

ENTITY counter3bit IS
  PORT (
  ------------------------------------------------------------------------------
  --Insert input ports below
    clock      : IN  std_logic;                    -- input bit example
    enable      : IN std_logic;
  ------------------------------------------------------------------------------
  --Insert output ports below
  	value	   : OUT std_logic_vector (2 downto 0)
    );
END counter3bit;

--------------------------------------------------------------------------------
--Complete your VHDL description below
--------------------------------------------------------------------------------

ARCHITECTURE TypeArchitecture OF counter3bit IS

BEGIN


process(clock)
	variable internal_state : natural range 0 to 7 := 0;
	begin
	if(clock'event AND clock='0' AND enable='1') then
		if(internal_state = 7) then
			internal_state := 0;
		else
			internal_state := internal_state + 1;
		end if;
	end if;
	value <= std_logic_vector(to_unsigned(internal_state,3));
end process;

END TypeArchitecture;

// VHDL entity dmux8to1, as the project stores it:
LIBRARY ieee;
USE ieee.std_logic_1164.all;

ENTITY dmux8to1 IS
  PORT (
  ------------------------------------------------------------------------------
  --Insert input ports below
    val        : IN  std_logic;
    sel		: IN  std_logic_vector(2 downto 0);
  ------------------------------------------------------------------------------
  --Insert output ports below
    y0		: OUT std_logic;
    y1		: OUT std_logic;
    y2		: OUT std_logic;
    y3		: OUT std_logic;
    y4		: OUT std_logic;
    y5		: OUT std_logic;
    y6		: OUT std_logic;
    y7		: OUT std_logic
    );
END dmux8to1;

--------------------------------------------------------------------------------
--Complete your VHDL description below
--------------------------------------------------------------------------------

ARCHITECTURE TypeArchitecture OF dmux8to1 IS
	
BEGIN

process(val,sel)
begin
	y0<='1';
	y1<='1';
	y2<='1';
	y3<='1';
	y4<='1';
	y5<='1';
	y6<='1';
	y7<='1';
	case sel is
	when "000" =>
		y0 <= val;
	when "001" =>
		y1 <= val;
	when "010" =>
		y2 <= val;
	when "011" =>
		y3 <= val;
	when "100" =>
		y4 <= val;
	when "101" =>
		y5 <= val;
	when "110" =>
		y6 <= val;
	when "111" =>
		y7 <= val;
	when others =>
		y0<='1';
		y1<='1';
		y2<='1';
		y3<='1';
		y4<='1';
		y5<='1';
		y6<='1';
		y7<='1';
	end case;
end process;

END TypeArchitecture;

// VHDL entity mux8to1_8bit, as the project stores it:
LIBRARY ieee;
USE ieee.std_logic_1164.all;

ENTITY mux8to1_8bit IS
  PORT (
  	in0	: IN std_logic_vector(7 downto 0);
  	in1	: IN std_logic_vector(7 downto 0);
  	in2	: IN std_logic_vector(7 downto 0);
  	in3	: IN std_logic_vector(7 downto 0);
  	in4	: IN std_logic_vector(7 downto 0);
  	in5	: IN std_logic_vector(7 downto 0);
  	in6	: IN std_logic_vector(7 downto 0);
  	in7	: IN std_logic_vector(7 downto 0);
  	sel  : IN std_logic_vector(2 downto 0);

	y	: OUT std_logic_vector(7 downto 0)
    );
END mux8to1_8bit;

--------------------------------------------------------------------------------
--Complete your VHDL description below
--------------------------------------------------------------------------------

ARCHITECTURE TypeArchitecture OF mux8to1_8bit IS
BEGIN

process(sel,in0,in1,in2,in3,in4,in5,in6,in7)
begin
	case sel is
	when "000" =>
		y <= in0;
	when "001" =>
		y <= in1;
	when "010" =>
		y <= in2;
	when "011" =>
		y <= in3;
	when "100" =>
		y <= in4;
	when "101" =>
		y <= in5;
	when "110" =>
		y <= in6;
	when "111" =>
		y <= in7;
	when others =>
		y<= (others => '0');
	end case;
end process;

END TypeArchitecture;

// VHDL entity shift_register_11bit, as the project stores it:
LIBRARY ieee;
USE ieee.std_logic_1164.all;

ENTITY shift_register_11bit IS
  PORT (
  ------------------------------------------------------------------------------
  --Insert input ports below
    clk      : IN  std_logic; --clk signal, synchronized to the ps2 clock               
    sin      : IN  std_logic; --serial input
    reset	   : IN 	std_logic;
  ------------------------------------------------------------------------------
  --Insert output ports below
    q	   :	OUT std_logic_vector(10 downto 0); --output of the register
    q8	   : OUT std_logic_vector(8 downto 1)
    );
END shift_register_11bit;

ARCHITECTURE TypeArchitecture OF shift_register_11bit IS

BEGIN

process(clk) is
variable reg : std_logic_vector(10 downto 0) := (others=>'0'); --variable to store the internal state of the register
begin
	if(clk'event AND clk='0') then --detecting fallin edge
		if(reset = '1') then
			reg := (others => '0');	
		else
			reg := sin & reg(10 downto 1);
		end if;
	end if;
	q <= reg;
	q8 <= reg(8 downto 1);
end process;	

END TypeArchitecture;

// VHDL entity modulo11_counter, as the project stores it:
LIBRARY ieee;
USE ieee.std_logic_1164.all;

ENTITY modulo11_counter IS
  PORT (
    clk	: IN  std_logic;--clock signal
    reset : IN std_logic;
    tc	: OUT std_logic--terminal count
    );
END modulo11_counter;

ARCHITECTURE TypeArchitecture OF modulo11_counter IS

BEGIN

process(clk) is
variable count : natural range 0 to 10 := 0;--internal state of the counter

begin
	if(clk'event AND clk='0') then --detecting the falling edge
		if(reset = '1') then
			count := 0;
			tc <= '0';
		elsif(count = 10) then
			count := 0;
			tc <= '1';
		else 
			count := count + 1;
			tc <= '0';
		end if;
	end if;
end process;
END TypeArchitecture;

// VHDL entity validation_unit, as the project stores it:
LIBRARY ieee;
USE ieee.std_logic_1164.all;

ENTITY validation_unit IS
  PORT (
  c		: IN std_logic_vector(10 downto 0);--code read from the keyboard
  valid 	: OUT std_logic
   );
END validation_unit;


ARCHITECTURE TypeArchitecture OF validation_unit IS
BEGIN
process(c)
variable parity : std_logic := '0';--here we store the parity of the 8 data bits
begin

	--calculate the parity of the data bits
	--for i in 1 to 9 loop--data bits are on position 1 to 8 of the code and pairty bit on 9
		parity := c(1) xor c(2) xor c(3) xor c(4) xor c(5) xor c(6) xor c(7) xor c(8) xor c(9);
	--end loop;
	--coditions for checking if the signal is valid
	if(c(0) = '0' AND C(10)='1' AND parity='1') then
		valid <= '1';
	else 
		valid <= '0';
	end if;
end process;
END TypeArchitecture;

// VHDL entity eo_verif_unit, as the project stores it:
LIBRARY ieee;
USE ieee.std_logic_1164.all;

ENTITY eo_verif_unit IS
  PORT (
  c		: IN std_logic_vector(10 downto 0);--code read from the keyboard
  valid 	: OUT std_logic
   );
END eo_verif_unit;


ARCHITECTURE TypeArchitecture OF eo_verif_unit IS
BEGIN
process(c)
begin
	if(c(8 downto 1) = x"E0") then
		valid <= '1';
	else
		valid <= '0';
	end if;
end process;
END TypeArchitecture;

// VHDL entity fo_verif_unit, as the project stores it:
LIBRARY ieee;
USE ieee.std_logic_1164.all;

ENTITY fo_verif_unit IS
  PORT (
  c		: IN std_logic_vector(10 downto 0);--code read from the keyboard
  valid 	: OUT std_logic
   );
END fo_verif_unit;


ARCHITECTURE TypeArchitecture OF fo_verif_unit IS
BEGIN
process(c)
begin
	if(c(8 downto 1) = x"F0") then
		valid <= '1';
	else
		valid <= '0';
	end if;
end process;
END TypeArchitecture;

// VHDL entity enter_verif_unit, as the project stores it:
LIBRARY ieee;
USE ieee.std_logic_1164.all;

ENTITY enter_verif_unit IS
  PORT (
  c		: IN std_logic_vector(10 downto 0);--code read from the keyboard
  valid 	: OUT std_logic
   );
END enter_verif_unit;


ARCHITECTURE TypeArchitecture OF enter_verif_unit IS
BEGIN
process(c)
begin
	if(c(8 downto 1) = x"5A") then
		valid <= '1';
	else
		valid <= '0';
	end if;
end process;
END TypeArchitecture;

// VHDL entity clk_sync, as the project stores it:
LIBRARY ieee;
USE ieee.std_logic_1164.all;

ENTITY clk_sync IS
  PORT (
  sys_clk : IN std_logic;
  ps2_clk : IN	std_logic;

  synced  : OUT std_logic
  );

END clk_sync;

ARCHITECTURE TypeArchitecture OF clk_sync IS

BEGIN
process(sys_clk) is
variable internal_state : std_logic_vector(7 downto 0) := (others => '0'); -- 8 bit shift register for sampling the ps2 clock signal
begin
	if(sys_clk'event AND sys_clk='0') then
		internal_state := ps2_clk & internal_state (7 downto 1);
	end if;
	if internal_state = "11111111" then
		synced <= '1';
	elsif internal_state = "00000000" then
		synced <= '0';
	end if;	
end process;

END TypeArchitecture;

// VHDL entity ps2_simulator, as the project stores it:
LIBRARY ieee;
USE ieee.std_logic_1164.all;

ENTITY ps2_simulator IS
  PORT (
	sys_clk : IN std_logic;
	ps2_ser : OUT std_logic;
	ps2_clk : OUT std_logic
    );
END ps2_simulator;


ARCHITECTURE TypeArchitecture OF ps2_simulator IS
signal continue : natural := 1;
BEGIN

ser: process(sys_clk)
variable code : std_logic_vector(10 downto 0) := "10000101100";
variable i : natural := 0;
begin
	if sys_clk'event and sys_clk='1' and i<11 then 
		ps2_ser <= code(i mod 11);
		i := i+1;
		if i = 10 then 
			continue <= 0;
		end if;
	end if;
end process ser;

clk: process(sys_clk)
begin
	if continue = 1 then
		ps2_clk <= sys_clk;
	end if;
end process clk;


END TypeArchitecture;

// VHDL entity ps2_simulator_bench, as the project stores it:
LIBRARY ieee;
USE ieee.std_logic_1164.all;

ENTITY ps2_simulator_bench IS
  PORT (
  
    max        : OUT std_logic;                    -- output bit example
    cpt        : OUT std_logic_vector(3 DOWNTO 0)  -- output vector example
    );
END ps2_simulator_bench;

--------------------------------------------------------------------------------
--Complete your VHDL description below
--------------------------------------------------------------------------------

ARCHITECTURE TypeArchitecture OF ps2_simulator_bench IS

BEGIN
process 
begin
	for i in 1 to 10 loop
		max<='0';
		wait for 10 ns;
		max<='1';
		wait for 10 ns;
	end loop;
wait;
end process;
END TypeArchitecture;
