// Logisim project ps2_interface_valpha.circ as structural Verilog
module main (
  input  reset,
  input  ps2_clk,
  input  ps2_ser
);

  wire clk_sync_1_synced, clock_1_out, counter16bit_1_tcount, cu_outputs_1_clear, cu_outputs_1_en_shift,
       eo_verif_unit_1_valid, modulo11_counter_1_tc, mux8to1whichis1bit_1_output, not_1_out,
       validation_unit_1_valid;
  wire [2:0] counter3bit_1_value, cu_rom_1_contents;
  wire [3:0] d_flip_flop_4_q;
  wire [7:0] and_1_out, display_buffer_1_data_out0, display_buffer_1_data_out1, display_buffer_1_data_out2,
       display_buffer_1_data_out3, display_buffer_1_data_out4, display_buffer_1_data_out5,
       display_buffer_1_data_out6, display_buffer_1_data_out7;
  wire [10:0] shift_register_11bit_1_q;

  Clock clock_1 (.out(clock_1_out));
  CU_ROM cu_rom_1 (.adress(d_flip_flop_4_q), .contents(cu_rom_1_contents));
  d_flip_flop d_flip_flop_1 (.clock(clock_1_out), .d(cu_rom_1_contents[0]), .q(d_flip_flop_4_q[0]));
  d_flip_flop d_flip_flop_2 (.clock(clock_1_out), .d(cu_rom_1_contents[1]), .q(d_flip_flop_4_q[1]));
  d_flip_flop d_flip_flop_3 (.clock(clock_1_out), .d(cu_rom_1_contents[2]), .q(d_flip_flop_4_q[2]));
  clk_sync clk_sync_1 (.sys_clk(clock_1_out), .ps2_clk(ps2_clk), .synced(clk_sync_1_synced));
  MUX8TO1WHICHIS1BIT mux8to1whichis1bit_1 (
    .val(and_1_out), .sel(d_flip_flop_4_q[2:0]), .\output (mux8to1whichis1bit_1_output));
  shift_register_11bit shift_register_11bit_1 (
    .clk(clk_sync_1_synced), .sin(ps2_ser), .reset(reset), .q(shift_register_11bit_1_q));
  modulo11_counter modulo11_counter_1 (.clk(clk_sync_1_synced), .reset(reset), .tc(modulo11_counter_1_tc));
  d_flip_flop d_flip_flop_4 (.clock(clock_1_out), .d(mux8to1whichis1bit_1_output), .q(d_flip_flop_4_q[3]));
  CU_Outputs cu_outputs_1 (.state(d_flip_flop_4_q[2:0]), .en_shift(cu_outputs_1_en_shift), .clear(cu_outputs_1_clear));
  validation_unit validation_unit_1 (.c(shift_register_11bit_1_q), .valid(validation_unit_1_valid));
  eo_verif_unit eo_verif_unit_1 (.c(shift_register_11bit_1_q), .valid(eo_verif_unit_1_valid));
  fo_verif_unit fo_verif_unit_1 (.c(shift_register_11bit_1_q), .valid(and_1_out[1]));
  enter_verif_unit enter_verif_unit_1 (.c(shift_register_11bit_1_q), .valid(and_1_out[2]));
  and and_1 (and_1_out[0], validation_unit_1_valid, not_1_out, modulo11_counter_1_tc);
  not not_1 (not_1_out, eo_verif_unit_1_valid);
  display_buffer display_buffer_1 (
    .data_in(shift_register_11bit_1_q[8:1]), .enable(cu_outputs_1_en_shift), .clk(clock_1_out),
    .reset(cu_outputs_1_clear), .data_out0(display_buffer_1_data_out0),
    .data_out1(display_buffer_1_data_out1), .data_out2(display_buffer_1_data_out2),
    .data_out3(display_buffer_1_data_out3), .data_out4(display_buffer_1_data_out4),
    .data_out5(display_buffer_1_data_out5), .data_out6(display_buffer_1_data_out6),
    .data_out7(display_buffer_1_data_out7));
  counter16bit counter16bit_1 (.clock(clock_1_out), .tCount(counter16bit_1_tcount));  // open: value
  counter3bit counter3bit_1 (.clock(clock_1_out), .enable(counter16bit_1_tcount), .value(counter3bit_1_value));
  mux8to1_8bit mux8to1_8bit_1 (
    .in0(display_buffer_1_data_out0), .in1(display_buffer_1_data_out1), .in2(display_buffer_1_data_out2),
    .in3(display_buffer_1_data_out3), .in4(display_buffer_1_data_out4), .in5(display_buffer_1_data_out5),
    .in6(display_buffer_1_data_out6), .in7(display_buffer_1_data_out7), .sel(counter3bit_1_value));  // open: y
  dmux8to1 dmux8to1_1 (.val(1'b0), .sel(counter3bit_1_value));  // open: y0, y1, y2, y3, y4, y5, y6, y7

  // Notes on the sheet:
  //   clk
endmodule

// VHDL entity CU_ROM, as the project stores it:
LIBRARY ieee;
USE ieee.std_logic_1164.all;

ENTITY CU_ROM IS
  PORT (
  	adress 	: IN std_logic_vector(3 downto 0);

  	contents	: OUT std_logic_vector(2 downto 0)
    );
END CU_ROM;

--------------------------------------------------------------------------------
--Complete your VHDL description below
--------------------------------------------------------------------------------

ARCHITECTURE TypeArchitecture OF CU_ROM IS
BEGIN

process(adress) is 
begin
	if adress = "0000" then
		contents <= "000";
	elsif adress = "1000" then
		contents <= "001";
	elsif adress = "0001" then
		contents <= "010";
	elsif adress = "1001" then
		contents <= "011";
	elsif adress = "0010" then
		contents <= "100";
	elsif adress = "1010" then
		contents <= "101";
	else
		contents <= "000";
	end if;
end process;

END TypeArchitecture;

// VHDL entity CU_Outputs, as the project stores it:
LIBRARY ieee;
USE ieee.std_logic_1164.all;

ENTITY CU_Outputs IS
  PORT (
	state 	: IN std_logic_vector(2 downto 0);
	en_shift 	: OUT std_logic;
	clear	: OUT std_logic
  );
END CU_Outputs;

ARCHITECTURE TypeArchitecture OF CU_Outputs IS

BEGIN

process(state) is
begin
	if state = "100" then 
		en_shift <= '1';
	else 
		en_shift <= '0';
	end if;
	if state = "101" then
		clear <= '1';
	else 
		clear <= '0';
	end if;
end process;
END TypeArchitecture;

// VHDL entity d_flip_flop, as the project stores it:
LIBRARY ieee;
USE ieee.std_logic_1164.all;

ENTITY d_flip_flop IS
  PORT (
  ------------------------------------------------------------------------------
  --Insert input ports below
    clock      : IN  std_logic;                    -- input bit example
    d        	: IN  std_logic; -- input vector example
  ------------------------------------------------------------------------------
  --Insert output ports below
    q        : OUT std_logic
    );
END d_flip_flop;

--------------------------------------------------------------------------------
--Complete your VHDL description below
--------------------------------------------------------------------------------

ARCHITECTURE TypeArchitecture OF d_flip_flop IS

BEGIN

	process(clock) is
	begin
		if(rising_edge(clock)) then
			q <= d;
		end if;
	end process;
END TypeArchitecture;

// VHDL entity MUX8TO1WHICHIS1BIT, as the project stores it:
LIBRARY ieee;
USE ieee.std_logic_1164.all;

ENTITY MUX8TO1WHICHIS1BIT IS
  PORT (
  ------------------------------------------------------------------------------
  --Insert input ports below
    val        : IN  std_logic_vector(7 DOWNTO 0); -- input vector example
    sel 		: IN  std_logic_vector(2 downto 0); -- selection bit
  ------------------------------------------------------------------------------
  --Insert output ports below
    output        : OUT std_logic                -- output bit example
    );
END MUX8TO1WHICHIS1BIT;

--------------------------------------------------------------------------------
--Complete your VHDL description below
--------------------------------------------------------------------------------

ARCHITECTURE TypeArchitecture OF MUX8TO1WHICHIS1BIT IS

BEGIN

	process(val, sel)
		begin
			case sel is
			when "000" => output <= val(0);
			when "001" => output <= val(1);
			when "010" => output <= val(2);
			when "011" => output <= val(3);
			when "100" => output <= val(4);
			when "101" => output <= val(5);
			when "110" => output <= val(6);
			when "111" => output <= val(7);
			when others => output <= '0';
	end case;

	end process;
END TypeArchitecture;

// VHDL entity decoder7sd, as the project stores it:
-- Project :
-- File    :
-- Autor   :
-- Date    :
--
--------------------------------------------------------------------------------
-- Description :
--
--------------------------------------------------------------------------------

LIBRARY ieee;
USE ieee.std_logic_1164.all;

ENTITY decoder7sd IS
  PORT (
  ------------------------------------------------------------------------------
  --Insert input ports below
    address      : IN  std_logic_vector (7 downto 0);                    -- input bit example
  ------------------------------------------------------------------------------
  --Insert output ports below
    content        : OUT std_logic_vector (7 DOWNTO 0)  -- output vector example
    );
END decoder7sd;

--------------------------------------------------------------------------------
--Complete your VHDL description below
--------------------------------------------------------------------------------

ARCHITECTURE TypeArchitecture OF decoder7sd IS
BEGIN

	process(address)
		begin
			case address is 
				when x"16" => content <= b"01100000"; --1
				when x"1E" => content <= b"11011010"; --2
				when x"26" => content <= b"11110010"; --3
				when x"25" => content <= b"01100110"; --4
				when x"2E" => content <= b"10110110"; --5
				when x"36" => content <= b"10111110"; --6
				when x"3D" => content <= b"11100000"; --7
				when x"3E" => content <= b"11111110"; --8
				when x"46" => content <= b"11110110"; --9
				when x"45" => content <= b"11111100"; --0
				when x"15" => content <= b"11111101"; --q
				when x"44" => content <= b"11111100"; --o
				when x"1D" => content <= b"01111110"; --w
				when x"24" => content <= b"10011110"; --e
				when x"2D" => content <= b"00001010"; --small r
				when x"2C" => content <= b"00011110"; --small t
				when x"35" => content <= b"01110110"; --small y
				when x"3C" => content <= b"01111100"; --U
				when x"43" => content <= b"00001100"; --I
				when x"4D" => content <= b"11001110"; --P
				when x"1C" => content <= b"11101110"; --A
				when x"1B" => content <= b"10110110"; --S
				when x"23" => content <= b"11111100"; --D
				when x"2B" => content <= b"10001110"; --F
				when x"34" => content <= b"10111100"; --G
				when x"33" => content <= b"01101110"; --H
				when x"3B" => content <= b"01111000"; --J
				when x"42" => content <= b"10101110"; --K 
				when x"4B" => content <= b"00011100"; --L
				when x"1A" => content <= b"00001100"; --Z
				when x"22" => content <= b"10010010"; --x
				when x"21" => content <= b"10011100"; --C
				when x"2A" => content <= b"01010100"; --V
				when x"32" => content <= b"11111110"; --B
				when x"31" => content <= b"00101010"; --small N
				when x"3A" => content <= b"11010100"; --M
				when x"41" => content <= b"00000001"; --,
				when x"49" => content <= b"00000001"; --.

				when others =>content<=  b"00000000"; 
		end case;
	end process;
END TypeArchitecture;

// VHDL entity display_buffer, as the project stores it:
LIBRARY ieee;
USE ieee.std_logic_1164.all;

ENTITY display_buffer IS
  PORT (
    data_in	: IN std_logic_vector(7 downto 0);
    enable	: IN std_logic;
    clk		: IN std_logic;
    reset		: IN std_logic;

    data_out0	: OUT std_logic_vector(7 downto 0);
    data_out1	: OUT std_logic_vector(7 downto 0);
    data_out2	: OUT std_logic_vector(7 downto 0);
    data_out3	: OUT std_logic_vector(7 downto 0);
    data_out4	: OUT std_logic_vector(7 downto 0);
    data_out5	: OUT std_logic_vector(7 downto 0);
    data_out6	: OUT std_logic_vector(7 downto 0);
    data_out7	: OUT std_logic_vector(7 downto 0)
    );
END display_buffer;


ARCHITECTURE TypeArchitecture OF display_buffer IS

type t_Memory is array (7 downto 0) of std_logic_vector(7 downto 0);--type of data to store the contents of the shift register

BEGIN


process(clk) is
variable reg : t_Memory := (others => "00000000");
begin
	if(clk'event AND clk='0') then
		if(reset = '1') then
			reg := (others => "00000000");
		elsif(enable = '1') then
			reg := data_in & reg(7 downto 1);
		end if;
		data_out0 <= reg(0);
		data_out1 <= reg(1);
		data_out2 <= reg(2);
		data_out3 <= reg(3);
		data_out4 <= reg(4);
		data_out5 <= reg(5);
		data_out6 <= reg(6);
		data_out7 <= reg(7);
		 
	end if;
end process;

END TypeArchitecture;

// VHDL entity counter16bit, as the project stores it:
LIBRARY ieee;
USE ieee.std_logic_1164.all;

USE IEEE.NUMERIC_STD.ALL;

ENTITY counter16bit IS
  PORT (
  ------------------------------------------------------------------------------
  --Insert input ports below
    clock      : IN  std_logic;                    -- input bit example
  ------------------------------------------------------------------------------
  --Insert output ports below
  	value	   : OUT std_logic_vector (15 downto 0);
    tCount        : OUT std_logic                    -- output bit example
    );
END counter16bit;

--------------------------------------------------------------------------------
--Complete your VHDL description below
--------------------------------------------------------------------------------

ARCHITECTURE TypeArchitecture OF counter16bit IS

BEGIN


process(clock)
	variable internal_state : natural range 0 to 2**16-1 := 0;
	begin
	if(clock'event AND clock='1') then
		if(internal_state = 65535) then
			tCount <= '1';
			internal_state := 0;
		else
			tCount <= '0';
			internal_state := internal_state + 1;
		end if;
	end if;
	value <= std_logic_vector(to_unsigned(internal_state,16));
end process;

END TypeArchitecture;

// VHDL entity counter3bit, as the project stores it:
LIBRARY ieee;
USE ieee.std_logic_1164.all;

USE IEEE.NUMERIC_STD.ALL;

ENTITY counter3bit IS
  PORT (
  ------------------------------------------------------------------------------
  --Insert input ports below
    clock      : IN  std_logic;                    -- input bit example
    enable      : IN std_logic;
  ------------------------------------------------------------------------------
  --Insert output ports below
  	value	   : OUT std_logic_vector (2 downto 0)
    );
END counter3bit;

--------------------------------------------------------------------------------
--Complete your VHDL description below
--------------------------------------------------------------------------------

ARCHITECTURE TypeArchitecture OF counter3bit IS

BEGIN


process(clock)
	variable internal_state : natural range 0 to 7 := 0;
	begin
	if(clock'event AND clock='0' AND enable='1') then
		if(internal_state = 7) then
			internal_state := 0;
		else
			internal_state := internal_state + 1;
		end if;
	end if;
	value <= std_logic_vector(to_unsigned(internal_state,3));
end process;

END TypeArchitecture;

// VHDL entity dmux8to1, as the project stores it:
LIBRARY ieee;
USE ieee.std_logic_1164.all;

ENTITY dmux8to1 IS
  PORT (
  ------------------------------------------------------------------------------
  --Insert input ports below
    val        : IN  std_logic;
    sel		: IN  std_logic_vector(2 downto 0);
  ------------------------------------------------------------------------------
  --Insert output ports below
    y0		: OUT std_logic;
    y1		: OUT std_logic;
    y2		: OUT std_logic;
    y3		: OUT std_logic;
    y4		: OUT std_logic;
    y5		: OUT std_logic;
    y6		: OUT std_logic;
    y7		: OUT std_logic
    );
END dmux8to1;

--------------------------------------------------------------------------------
--Complete your VHDL description below
--------------------------------------------------------------------------------

ARCHITECTURE TypeArchitecture OF dmux8to1 IS
	
BEGIN

process(val,sel)
begin
	y0<='1';
	y1<='1';
	y2<='1';
	y3<='1';
	y4<='1';
	y5<='1';
	y6<='1';
	y7<='1';
	case sel is
	when "000" =>
		y0 <= val;
	when "001" =>
		y1 <= val;
	when "010" =>
		y2 <= val;
	when "011" =>
		y3 <= val;
	when "100" =>
		y4 <= val;
	when "101" =>
		y5 <= val;
	when "110" =>
		y6 <= val;
	when "111" =>
		y7 <= val;
	when others =>
		y0<='1';
		y1<='1';
		y2<='1';
		y3<='1';
		y4<='1';
		y5<='1';
		y6<='1';
		y7<='1';
	end case;
end process;

END TypeArchitecture;

// VHDL entity mux8to1_8bit, as the project stores it:
LIBRARY ieee;
USE ieee.std_logic_1164.all;

ENTITY mux8to1_8bit IS
  PORT (
  	in0	: IN std_logic_vector(7 downto 0);
  	in1	: IN std_logic_vector(7 downto 0);
  	in2	: IN std_logic_vector(7 downto 0);
  	in3	: IN std_logic_vector(7 downto 0);
  	in4	: IN std_logic_vector(7 downto 0);
  	in5	: IN std_logic_vector(7 downto 0);
  	in6	: IN std_logic_vector(7 downto 0);
  	in7	: IN std_logic_vector(7 downto 0);
  	sel  : IN std_logic_vector(2 downto 0);

	y	: OUT std_logic_vector(7 downto 0)
    );
END mux8to1_8bit;

--------------------------------------------------------------------------------
--Complete your VHDL description below
--------------------------------------------------------------------------------

ARCHITECTURE TypeArchitecture OF mux8to1_8bit IS
BEGIN

process(sel,in0,in1,in2,in3,in4,in5,in6,in7)
begin
	case sel is
	when "000" =>
		y <= in0;
	when "001" =>
		y <= in1;
	when "010" =>
		y <= in2;
	when "011" =>
		y <= in3;
	when "100" =>
		y <= in4;
	when "101" =>
		y <= in5;
	when "110" =>
		y <= in6;
	when "111" =>
		y <= in7;
	when others =>
		y<= (others => '0');
	end case;
end process;

END TypeArchitecture;

// VHDL entity shift_register_11bit, as the project stores it:
LIBRARY ieee;
USE ieee.std_logic_1164.all;

ENTITY shift_register_11bit IS
  PORT (
  ------------------------------------------------------------------------------
  --Insert input ports below
    clk      : IN  std_logic; --clk signal, synchronized to the ps2 clock               
    sin      : IN  std_logic; --serial input
    reset	   : IN 	std_logic;
  ------------------------------------------------------------------------------
  --Insert output ports below
    q	   :	OUT std_logic_vector(10 downto 0) --output of the register
    );
END shift_register_11bit;

ARCHITECTURE TypeArchitecture OF shift_register_11bit IS

BEGIN

process(clk) is
variable reg : std_logic_vector(10 downto 0) := (others=>'0'); --variable to store the internal state of the register
begin
	if(clk'event AND clk='0') then --detecting fallin edge
		if(reset = '1') then
			reg := (others => '0');	
		else
			reg := sin & reg(10 downto 1);
		end if;
	end if;
	q <= reg;
end process;	

END TypeArchitecture;

// VHDL entity modulo11_counter, as the project stores it:
LIBRARY ieee;
USE ieee.std_logic_1164.all;

ENTITY modulo11_counter IS
  PORT (
    clk	: IN  std_logic;--clock signal
    reset : IN std_logic;
    tc	: OUT std_logic--terminal count
    );
END modulo11_counter;

ARCHITECTURE TypeArchitecture OF modulo11_counter IS

BEGIN

process(clk) is
variable count : natural range 0 to 10 := 0;--internal state of the counter

begin
	if(clk'event AND clk='0') then --detecting the falling edge
		if(reset = '1') then
			count := 0;
			tc <= '0';
		elsif(count = 10) then
			count := 0;
			tc <= '1';
		else 
			count := count + 1;
			tc <= '0';
		end if;
	end if;
end process;
END TypeArchitecture;

// VHDL entity validation_unit, as the project stores it:
LIBRARY ieee;
USE ieee.std_logic_1164.all;

ENTITY validation_unit IS
  PORT (
  c		: IN std_logic_vector(10 downto 0);--code read from the keyboard
  valid 	: OUT std_logic
   );
END validation_unit;


ARCHITECTURE TypeArchitecture OF validation_unit IS
BEGIN
process(c)
variable parity : std_logic := '0';--here we store the parity of the 8 data bits
begin

	--calculate the parity of the data bits
	--for i in 1 to 9 loop--data bits are on position 1 to 8 of the code and pairty bit on 9
		parity := c(1) xor c(2) xor c(3) xor c(4) xor c(5) xor c(6) xor c(7) xor c(8) xor c(9);
	--end loop;
	--coditions for checking if the signal is valid
	if(c(0) = '0' AND C(10)='1' AND parity='1') then
		valid <= '1';
	else 
		valid <= '0';
	end if;
end process;
END TypeArchitecture;

// VHDL entity eo_verif_unit, as the project stores it:
LIBRARY ieee;
USE ieee.std_logic_1164.all;

ENTITY eo_verif_unit IS
  PORT (
  c		: IN std_logic_vector(10 downto 0);--code read from the keyboard
  valid 	: OUT std_logic
   );
END eo_verif_unit;


ARCHITECTURE TypeArchitecture OF eo_verif_unit IS
BEGIN
process(c)
begin
	if(c(8 downto 1) = x"E0") then
		valid <= '1';
	else
		valid <= '0';
	end if;
end process;
END TypeArchitecture;

// VHDL entity fo_verif_unit, as the project stores it:
LIBRARY ieee;
USE ieee.std_logic_1164.all;

ENTITY fo_verif_unit IS
  PORT (
  c		: IN std_logic_vector(10 downto 0);--code read from the keyboard
  valid 	: OUT std_logic
   );
END fo_verif_unit;


ARCHITECTURE TypeArchitecture OF fo_verif_unit IS
BEGIN
process(c)
begin
	if(c(8 downto 1) = x"F0") then
		valid <= '1';
	else
		valid <= '0';
	end if;
end process;
END TypeArchitecture;

// VHDL entity enter_verif_unit, as the project stores it:
LIBRARY ieee;
USE ieee.std_logic_1164.all;

ENTITY enter_verif_unit IS
  PORT (
  c		: IN std_logic_vector(10 downto 0);--code read from the keyboard
  valid 	: OUT std_logic
   );
END enter_verif_unit;


ARCHITECTURE TypeArchitecture OF enter_verif_unit IS
BEGIN
process(c)
begin
	if(c(8 downto 1) = x"5A") then
		valid <= '1';
	else
		valid <= '0';
	end if;
end process;
END TypeArchitecture;

// VHDL entity clk_sync, as the project stores it:
LIBRARY ieee;
USE ieee.std_logic_1164.all;

ENTITY clk_sync IS
  PORT (
  sys_clk : IN std_logic;
  ps2_clk : IN	std_logic;

  synced  : OUT std_logic
  );

END clk_sync;

ARCHITECTURE TypeArchitecture OF clk_sync IS

BEGIN
process(sys_clk) is
variable internal_state : std_logic_vector(7 downto 0) := (others => '0'); -- 8 bit shift register for sampling the ps2 clock signal
begin
	if(sys_clk'event AND sys_clk='0') then
		internal_state := ps2_clk & internal_state (7 downto 1);
	end if;
	if internal_state = "11111111" then
		synced <= '1';
	elsif internal_state = "00000000" then
		synced <= '0';
	end if;	
end process;

END TypeArchitecture;

// VHDL entity clk_sync_tb, as the project stores it:
LIBRARY ieee;
USE ieee.std_logic_1164.all;

ENTITY clk_sync_tb IS
END clk_sync_tb;

--test bench for the filter
ARCHITECTURE TypeArchitecture OF clk_sync_tb IS

--signal declaration
signal 
sys_clk : std_logic;
signal ps2_clk : std_logic;
signal synced  : std_logic;

--component declaration
component clk_sync is
  PORT (
  sys_clk :  std_logic;
  ps2_clk :  std_logic;
  synced  : std_logic
  );
end component clk_sync;

BEGIN

UUT: clk_sync 
	port map(
	  sys_clk=>sys_clk,
	  ps2_clk=>ps2_clk,
	  synced=>synced
	);

process
variable code1 : std_logic_vector(8 downto 0) := (others => '1');
variable code2 : std_logic_vector(8 downto 0) := (others => '0');

begin
	wait;
end process;

END TypeArchitecture;

// VHDL entity ghkj, as the project stores it:
--------------------------------------------------------------------------------
-- Project :
-- File    :
-- Autor   :
-- Date    :
--
--------------------------------------------------------------------------------
-- Description :
--
--------------------------------------------------------------------------------

LIBRARY ieee;
USE ieee.std_logic_1164.all;

ENTITY ghkj IS
  PORT (
  ------------------------------------------------------------------------------
  --Insert input ports below
    clock      : IN  std_logic;                    -- input bit example
    val        : IN  std_logic_vector(3 DOWNTO 0); -- input vector example
  ------------------------------------------------------------------------------
  --Insert output ports below
    max        : OUT std_logic;                    -- output bit example
    cpt        : OUT std_logic_vector(3 DOWNTO 0)  -- output vector example
    );
END ghkj;

--------------------------------------------------------------------------------
--Complete your VHDL description below
--------------------------------------------------------------------------------

ARCHITECTURE TypeArchitecture OF ghkj IS

BEGIN


END TypeArchitecture;
